// Logisim project Automated Streetlight.circ as structural Verilog: 1 circuit, main circuit main
module main (
  input  PIR_sensor,
  input  LDR_sensor
);

  wire and_1_out;

  LED led_1 (.in(and_1_out));
  and and_1 (and_1_out, PIR_sensor, LDR_sensor);
endmodule
